# Fritzing sketch avoidance (saved by Fritzing 0.9.2b)
breadboards: 1

parts:
  Part1 = Arduino Nano (Rev3.0)
  LIPO_3_7V_Battery = LIPO-110mAh [package=lipo-110]
  Screw_Terminal_(B) = Screw terminal - 2 pins [package=THT]
  Right_Motor = DC Motor
  Screw_Terminal_(A) = Screw terminal - 2 pins [package=THT]
  Left_Motor = DC Motor
  Part2 = SRF05 Ultrasonic Rangefinder

nets:
  GND: Part1.GND, LIPO_3_7V_Battery.-, Part2.GND
  B-1A: Part1.D6
  B-1B: Part1.D7
  A-1B: Part1.D8
  A-1A: Part1.D9
  N1: Part1.D10, Part2.Trig, Part2.Echo
  VCC: LIPO_3_7V_Battery.+, Part2.VCC
  N2: Screw_Terminal_(B).pin1, Left_Motor.pin_1
  N3: Screw_Terminal_(B).pin2, Left_Motor.pin_2
  N4: Right_Motor.pin_1, Screw_Terminal_(A).pin1
  N5: Right_Motor.pin_2, Screw_Terminal_(A).pin2

notes:
  Motor Controller Pins
