# Fritzing sketch motor_with_bt (saved by Fritzing 0.9.2b)
breadboards: 1

parts:
  Part1 = Arduino Nano (Rev3.0)
  LIPO_3_7V_Battery = LIPO-110mAh [package=lipo-110]
  Screw_Terminal_(B) = Screw terminal - 2 pins [package=THT]
  Right_Motor = DC Motor
  Screw_Terminal_(A) = Screw terminal - 2 pins [package=THT]
  Left_Motor = DC Motor

nets:
  BT RX: Part1.D1/TX
  BT TX: Part1.D0/RX
  BT GND/GND: Part1.GND, LIPO_3_7V_Battery.-
  B-1A: Part1.D6
  B-1B: Part1.D7
  A-1B: Part1.D8
  A-1A: Part1.D9
  BT VCC/VCC: Part1.5V, LIPO_3_7V_Battery.+
  N1: Screw_Terminal_(B).pin1, Left_Motor.pin_1
  N2: Screw_Terminal_(B).pin2, Left_Motor.pin_2
  N3: Right_Motor.pin_1, Screw_Terminal_(A).pin1
  N4: Right_Motor.pin_2, Screw_Terminal_(A).pin2

notes:
  Motor Controller Pins
  Bluetooth Module
