# Fritzing sketch basic_wiring (saved by Fritzing 0.8.7b)
breadboards: 1

parts:
  Nano = Arduino Nano (Rev3.0)
  VCC1 = 4 x AAA Battery Mount
  L_Servo = Basic Servo
  R_Servo = Basic Servo

nets:
  GND: Nano.GND, VCC1.-, L_Servo.gnd, R_Servo.gnd
  N1: Nano.D8, R_Servo.pulse
  N2: Nano.D9, L_Servo.pulse
  VCC: VCC1.+, L_Servo.vcc, R_Servo.vcc
