# Fritzing sketch simplebotpcb (saved by Fritzing 0.8.7b)
circuit board: 6.9215cm x 5.33756cm
breadboards: 1

parts:
  7 = Basic Servo
  8 = Basic Servo
  9 = Basic Servo
  10 = Basic Servo
  Nano_(D1) = Arduino Nano (Rev3.0)
  Servo_Batt = Battery
  BT = female pin header, 6 pins [form="♀ (female)"]
  WiFi(1) = female pin header, 10 pins [form="♀ (female)"]
  Sonic_(+) = female pin header, 4 pins [form="♀ (female)"]
  Uno = Arduino Uno (Rev3) - ICSP

nets:
  GND: 7.gnd, 8.gnd, 9.gnd, 10.gnd, Nano_(D1).GND, Servo_Batt.-, BT.pin4, WiFi(1).pin1, Sonic_(+).pin4, Uno.GND
  VCC: 7.vcc, 8.vcc, 9.vcc, 10.vcc, Servo_Batt.+
  N1: 7.pulse, Nano_(D1).D7, Uno.D7
  N2: 8.pulse, Nano_(D1).D8, Uno.D8
  N3: 9.pulse, Nano_(D1).D9, Uno.D9_PWM
  N4: 10.pulse, Nano_(D1).D10, Uno.D10_PWM/SS
  N5: Nano_(D1).D1/TX, BT.pin2, WiFi(1).pin5, Uno.D1/TX
  N6: Nano_(D1).D0/RX, BT.pin3, WiFi(1).pin6, Uno.D0/RX
  N7: Nano_(D1).RESET, Uno.RESET
  N8: Nano_(D1).D2, Uno.D2
  N9: Nano_(D1).D3, Uno.D3_PWM
  N10: Nano_(D1).D4, Uno.D4
  N11: Nano_(D1).D5, Uno.D5_PWM
  N12: Nano_(D1).D6, Sonic_(+).pin2, Sonic_(+).pin3, Uno.D6_PWM
  N13: Nano_(D1).D11/MOSI, Uno.ICSP_MOSI, Uno.D11_PWM/MOSI
  N14: Nano_(D1).D12/MISO, Uno.ICSP_MISO, Uno.D12/MISO
  VIN: Nano_(D1).VIN, Uno.VIN
  5V: Nano_(D1).5V, BT.pin5, Sonic_(+).pin1, Uno.5V
  N15: Nano_(D1).A5, Uno.A5/SCL
  N16: Nano_(D1).A4, Uno.A4/SDA
  N17: Nano_(D1).A3, Uno.A3
  N18: Nano_(D1).A2, Uno.A2
  N19: Nano_(D1).A1, Uno.A1
  N20: Nano_(D1).A0, Uno.A0
  3V3: Nano_(D1).3V3, WiFi(1).pin2, Uno.3V3
  N21: Nano_(D1).D13/SCK, Uno.ICSP_SCK, Uno.D13/SCK

notes:
  Servos
  +
  SimpleBot Shield V2.5
  GND
  5V
  3V3
  TX
  RX
  design: @ajfisher
  rev 3
